# Fritzing sketch skate-judge-direct-lipo (saved by Fritzing 1.0.5)

parts:
  U1_·_Feather_ESP32-S3 = adafruit
  U2_·_LSM6DSO32 = adafruit
  LED1_·_8-pixel_RGB_stick = adafruit
  R1_·_330_Ω = Resistor [resistance=330 tolerance=±5% power=0.25 package=THT]
  BAT1_·_1S_LiPo = skate-judge-lipo

nets:
  N1: U1_·_Feather_ESP32-S3.connector29, U2_·_LSM6DSO32.connector11
  N2: U1_·_Feather_ESP32-S3.connector30, U2_·_LSM6DSO32.connector12
  N3: U1_·_Feather_ESP32-S3.connector31, U2_·_LSM6DSO32.connector13
  N4: U1_·_Feather_ESP32-S3.connector32, U2_·_LSM6DSO32.connector14
  N5: U1_·_Feather_ESP32-S3.connector60, LED1_·_8-pixel_RGB_stick.connector26
  N6: U1_·_Feather_ESP32-S3.connector64, LED1_·_8-pixel_RGB_stick.connector24
  N7: U1_·_Feather_ESP32-S3.connector73, R1_·_330_Ω.Pin_0
  N8: U1_·_Feather_ESP32-S3.connector217, BAT1_·_1S_LiPo.connector1
  N9: U1_·_Feather_ESP32-S3.connector218, BAT1_·_1S_LiPo.connector0
  N10: LED1_·_8-pixel_RGB_stick.connector25, R1_·_330_Ω.Pin_1

notes:
  SKATE JUDGE — DIRECT-LiPo FIRST PROTOTYPE
  Editable wiring layout · power disconnected while wiring · not a production PCB design
  ONE STEMMA QT CABLE
  Red: switched 3.3 V · black: GND · blue: SDA / GPIO3 · yellow: SCL / GPIO4. GPIO7 enables this rail; no extra wire.
  LED STICK
  GPIO5 (pad marked 5) is DATA, not 5 V. R1: recommended 330 Ω, near DIN. DOUT is unconnected. BAT supplies battery voltage, not regulated 5 V.
  CHECK BEFORE SKATING
  Direct LiPo is a bench-test option: this RGB stick is specified for 4–7 V, so operation below 4 V is not guaranteed. Test fully charged and partly discharged. Verify JST polarity. Insulate and protect the battery. Crossings without a junction are not connections.
